# Fritzing sketch maquette (saved by Fritzing 0.8.3b)
breadboards: 1

parts:
  Composants1 = Arduino Mega 2560 (Rev3)
  S2 = Pushbutton [package=THT]
  C1 = Ceramic Capacitor [capacitance=100nF package="100 mil [THT, multilayer]"]
  LED1 = LED - 5mm [color="Red (633nm)" package="5 mm [THT]"]
  R4 = Resistor [tolerance=±20% resistance=150 package=THT]
  LED2 = LED - 5mm [color="Red (633nm)" package="5 mm [THT]"]
  R5 = Resistor [tolerance=±5% resistance=150 package=THT]
  LED3 = LED - 5mm [color="Red (633nm)" package="5 mm [THT]"]
  R6 = Resistor [tolerance=±5% resistance=150 package=THT]
  S7 = Pushbutton [package=THT]
  C5 = Ceramic Capacitor [capacitance=100nF package="100 mil [THT, multilayer]"]
  S8 = Pushbutton [package=THT]
  C6 = Ceramic Capacitor [capacitance=100nF package="100 mil [THT, multilayer]"]
  S9 = Pushbutton [package=THT]
  C7 = Ceramic Capacitor [capacitance=100nF package="100 mil [THT, multilayer]"]

nets:
  N1: Composants1.D20/SDA, Composants1.SDA, S2.leg1, C1.1
  N2: Composants1.D19/RX1, S7.leg1, C5.1
  N3: Composants1.5V, LED1.anode, LED2.anode, LED3.anode
  N4: Composants1.GND, S2.leg0, C1.0, S7.leg0, C5.0, S8.leg0, C6.0, S9.leg0, C7.0
  N5: Composants1.D2_PWM, S8.leg1, C6.1
  N6: Composants1.D3_PWM, S9.leg1, C7.1
  N7: Composants1.D5_PWM, R4.Pin_1
  N8: Composants1.D6_PWM, R5.Pin_1
  N9: Composants1.D7_PWM, R6.Pin_1
  N10: LED1.cathode, R4.Pin_0
  N11: LED2.cathode, R5.Pin_0
  N12: LED3.cathode, R6.Pin_0

notes:
  Boutons: Remise à Zéro, J1, J2, J3
  LEDs: J1, J2, J3
